# Fritzing sketch breadboard (saved by Fritzing 0.9.2b)
breadboards: 1

parts:
  Part2 = Sunny Buddy MPPT LiPo Charger
  U1 = MAX1704X [package=tdfn-8]
  BAT1 = LIPO-110mAh [package=lipo-110]  # not connected
  Part3 = Arduino Pro Mini v13
  R2 = Resistor [tolerance=±5% resistance=10k package=THT]
  Q1 = Basic FET P-Channel [package="TO220 [THT]"]
  Part4 = Pololu 9V Step-Up Voltage Regulator [part_number=U3V12F9]
  R1 = Resistor [tolerance=±5% resistance=10k package=THT]

nets:
  N1: Part2.Load_+_(Screw_Terminal), U1.CELL, U1.VDD, Part3.RAW, Q1.source
  GND: Part2.Load_-_(Screw_Terminal), U1.GND, Part3.GND, Part4.GND
  N2: U1.SCL, Part3.A5, R1.Pin_0
  N3: U1.SDA, Part3.A4, R2.Pin_0
  N4: Part3.VCC, R2.Pin_1, R1.Pin_1
  N5: Part3.D10_PWM/SS, Q1.gate
  N6: Q1.drain, Part4.VIN

custom parts:
  Sunny Buddy MPPT LiPo Charger: Switch-mode MPPT charger for single cell LiPo batteries. Accepts up to 20V solar cell input.
  Pololu 9V Step-Up Voltage Regulator: Description: The compact (0.32″×0.515″) U3V12F9 switching step-up (or boost) voltage regulator takes an input voltage as low as 2.5 V and efficiently boosts it to 9 V. The pins have a 0.1″ spacing, making this board compatible with standard solderless breadboards and perfboards. URL: https://www.pololu.com/product/2116
